// Logisim project sample group 20.circ as structural Verilog: 4 circuits, main circuit Main
module ALU (
  input  [15:0] A,
  input  [15:0] B,
  input  [2:0] alu_select,
  input  carry_in_adder,
  input  carry_in_sub,
  input  [15:0] multiply_carry_in,
  input  [15:0] divider_carry_in,
  output [15:0] alu_output,
  output carry_out_adder,
  output carry_out_sub,
  output [15:0] multiply_carry_out,
  output [15:0] divider_Carry_out
);

  wire [15:0] adder_1_out, and_1_out, divider_1_out, multiplier_1_out, nor_1_out, not_1_out, or_1_out,
       subtractor_1_out;

  assign and_1_out = A & B;  // AND_Gate and_1, 16 bits wide
  assign not_1_out = ~A;  // NOT_Gate not_1, 16 bits wide
  assign or_1_out = A | B;  // OR_Gate or_1, 16 bits wide
  assign nor_1_out = ~(A | B);  // NOR_Gate nor_1, 16 bits wide
  Adder #(.width(16)) adder_1 (.a(A), .b(B), .out(adder_1_out), .cin(carry_in_adder), .cout(carry_out_adder));
  Subtractor #(.width(16)) subtractor_1 (
    .a(A), .b(B), .out(subtractor_1_out), .bin(carry_in_sub), .bout(carry_out_sub));
  Multiplier #(.width(16)) multiplier_1 (
    .a(A), .b(B), .out(multiplier_1_out), .cin(multiply_carry_in), .cout(multiply_carry_out));
  Divider #(.width(16)) divider_1 (
    .a(A), .b(B), .out(divider_1_out), .upper(divider_carry_in), .rem(divider_Carry_out));
  Multiplexer #(.select(3), .width(16), .enable("false")) multiplexer_1 (
    .in0(and_1_out), .in1(not_1_out), .in2(or_1_out), .in3(nor_1_out), .in4(adder_1_out),
    .in5(subtractor_1_out), .in6(multiplier_1_out), .in7(divider_1_out), .out(alu_output), .sel(alu_select));
endmodule

module register_bank (
  input  [3:0] Write_Register,
  input  [15:0] Write_data,
  input  [3:0] Select_Ra_1,
  input  [3:0] Select_Ra_2,
  input  Write_enable,
  input  clock,
  output [15:0] Rd_1,
  output [15:0] Rd_2
);

  wire and_1_out, and_2_out, and_3_out, and_4_out, and_5_out, and_6_out, and_7_out, and_8_out, and_9_out,
       and_10_out, and_11_out, and_12_out, and_13_out, and_14_out, and_15_out, and_16_out, decoder_1_out0,
       decoder_1_out1, decoder_1_out2, decoder_1_out3, decoder_1_out4, decoder_1_out5, decoder_1_out6,
       decoder_1_out7, decoder_1_out8, decoder_1_out9, decoder_1_out10, decoder_1_out11, decoder_1_out12,
       decoder_1_out13, decoder_1_out14, decoder_1_out15;
  wire [15:0] _0_q, _1_q, _2_q, _3_q, _4_q, _5_q, _6_q, _7_q, _8_q, _9_q, _10_q, _11_q, _12_q, _13_q, _14_q,
       _15_q;

  Decoder #(.select(4), .enable("false")) decoder_1 (
    .out0(decoder_1_out0), .out1(decoder_1_out1), .out2(decoder_1_out2), .out3(decoder_1_out3),
    .out4(decoder_1_out4), .out5(decoder_1_out5), .out6(decoder_1_out6), .out7(decoder_1_out7),
    .out8(decoder_1_out8), .out9(decoder_1_out9), .out10(decoder_1_out10), .out11(decoder_1_out11),
    .out12(decoder_1_out12), .out13(decoder_1_out13), .out14(decoder_1_out14), .out15(decoder_1_out15),
    .sel(Write_Register));
  and and_1 (and_1_out, decoder_1_out0, Write_enable);
  and and_2 (and_2_out, decoder_1_out1, Write_enable);
  and and_3 (and_3_out, decoder_1_out2, Write_enable);
  and and_4 (and_4_out, decoder_1_out3, Write_enable);
  and and_5 (and_5_out, decoder_1_out4, Write_enable);
  and and_6 (and_6_out, decoder_1_out5, Write_enable);
  and and_7 (and_7_out, decoder_1_out6, Write_enable);
  and and_8 (and_8_out, decoder_1_out7, Write_enable);
  Register #(.width(16)) _0 (.D(Write_data), .en(and_1_out), .Q(_0_q), .clk(clock));  // open: clr
  Register #(.width(16)) _1 (.D(Write_data), .en(and_2_out), .Q(_1_q), .clk(clock));  // open: clr
  Register #(.width(16)) _2 (.D(Write_data), .en(and_3_out), .Q(_2_q), .clk(clock));  // open: clr
  Register #(.width(16)) _3 (.D(Write_data), .en(and_4_out), .Q(_3_q), .clk(clock));  // open: clr
  Register #(.width(16)) _4 (.D(Write_data), .en(and_5_out), .Q(_4_q), .clk(clock));  // open: clr
  Register #(.width(16)) _5 (.D(Write_data), .en(and_6_out), .Q(_5_q), .clk(clock));  // open: clr
  Register #(.width(16)) _6 (.D(Write_data), .en(and_7_out), .Q(_6_q), .clk(clock));  // open: clr
  Register #(.width(16)) _7 (.D(Write_data), .en(and_8_out), .Q(_7_q), .clk(clock));  // open: clr
  and and_9 (and_9_out, decoder_1_out8, Write_enable);
  and and_10 (and_10_out, decoder_1_out9, Write_enable);
  and and_11 (and_11_out, decoder_1_out10, Write_enable);
  and and_12 (and_12_out, decoder_1_out11, Write_enable);
  and and_13 (and_13_out, decoder_1_out12, Write_enable);
  and and_14 (and_14_out, decoder_1_out13, Write_enable);
  and and_15 (and_15_out, decoder_1_out14, Write_enable);
  and and_16 (and_16_out, decoder_1_out15, Write_enable);
  Register #(.width(16)) _8 (.D(Write_data), .en(and_9_out), .Q(_8_q), .clk(clock));  // open: clr
  Register #(.width(16)) _9 (.D(Write_data), .en(and_10_out), .Q(_9_q), .clk(clock));  // open: clr
  Register #(.width(16)) _10 (.D(Write_data), .en(and_11_out), .Q(_10_q), .clk(clock));  // open: clr
  Register #(.width(16)) _11 (.D(Write_data), .en(and_12_out), .Q(_11_q), .clk(clock));  // open: clr
  Register #(.width(16)) _12 (.D(Write_data), .en(and_13_out), .Q(_12_q), .clk(clock));  // open: clr
  Register #(.width(16)) _13 (.D(Write_data), .en(and_14_out), .Q(_13_q), .clk(clock));  // open: clr
  Register #(.width(16)) _14 (.D(Write_data), .en(and_15_out), .Q(_14_q), .clk(clock));  // open: clr
  Register #(.width(16)) _15 (.D(Write_data), .en(and_16_out), .Q(_15_q), .clk(clock));  // open: clr
  Multiplexer #(.select(4), .width(16), .enable("false")) multiplexer_1 (
    .in0(_0_q), .in1(_1_q), .in2(_2_q), .in3(_3_q), .in4(_4_q), .in5(_5_q), .in6(_6_q), .in7(_7_q),
    .in8(_8_q), .in9(_9_q), .in10(_10_q), .in11(_11_q), .in12(_12_q), .in13(_13_q), .in14(_14_q),
    .in15(_15_q), .out(Rd_1), .sel(Select_Ra_1));
  Multiplexer #(.select(4), .width(16), .enable("false")) multiplexer_2 (
    .in0(_0_q), .in1(_1_q), .in2(_2_q), .in3(_3_q), .in4(_4_q), .in5(_5_q), .in6(_6_q), .in7(_7_q),
    .in8(_8_q), .in9(_9_q), .in10(_10_q), .in11(_11_q), .in12(_12_q), .in13(_13_q), .in14(_14_q),
    .in15(_15_q), .out(Rd_2), .sel(Select_Ra_2));
endmodule

module control_unit (
  input  I_15,
  input  I_14,
  input  I_13,
  input  I_12,
  output AS1,
  output AS2,
  output AS3,
  output SA_SELECT,
  output WD_SELECT,
  output WE,
  output offset_select,
  output mem_write,
  output BRANCH,
  output BRANCH_SELECT,
  output Jump_select,
  output Imm_select
);

  wire and_1_out, and_2_out, and_3_out, and_4_out, and_5_out, and_6_out, and_7_out, and_8_out, and_9_out,
       and_10_out, and_11_out, and_12_out, and_13_out, and_14_out, and_15_out, and_16_out, and_17_out,
       and_18_out, and_19_out, and_20_out, and_21_out, and_22_out, and_23_out, and_24_out, and_25_out,
       and_26_out, and_27_out, and_28_out, and_29_out, and_30_out, and_31_out, and_32_out, and_33_out,
       and_34_out, and_35_out, and_36_out, and_37_out, and_38_out, and_39_out, nand_1_out, nand_2_out,
       nand_3_out, nand_4_out, nand_5_out, nand_6_out, nand_7_out, nand_9_out, nand_10_out, nand_11_out,
       nand_12_out, nand_13_out, nand_14_out, nand_15_out, nand_16_out, nand_17_out, nand_18_out,
       nand_19_out, nand_20_out, not_1_out, not_2_out, not_3_out, not_4_out, not_5_out, not_6_out, not_7_out,
       not_8_out, not_9_out, not_10_out, not_11_out, not_12_out, not_13_out, not_14_out, not_15_out,
       or_1_out, or_2_out, or_6_out;

  nand nand_1 (nand_1_out, I_14, I_14);
  nand nand_2 (nand_2_out, I_15, I_15);
  not not_1 (not_1_out, I_15);
  and and_1 (and_1_out, I_14, I_13);
  not not_2 (not_2_out, I_13);
  not not_3 (not_3_out, I_12);
  nand nand_3 (nand_3_out, I_14, I_14);
  nand nand_4 (nand_4_out, I_14, I_14);
  nand nand_5 (nand_5_out, I_13, I_13);
  nand nand_6 (nand_6_out, I_14, I_14);
  nand nand_7 (nand_7_out, I_13, I_13);
  not not_4 (not_4_out, I_14);
  and and_2 (and_2_out, not_4_out, not_5_out);
  not not_5 (not_5_out, I_13);
  not not_6 (not_6_out, I_12);
  not not_7 (not_7_out, I_15);
  and and_3 (and_3_out, not_7_out, I_12);
  not not_8 (not_8_out, I_14);
  and and_4 (and_4_out, not_8_out, I_12);
  and and_5 (and_5_out, I_15, not_9_out);
  not not_9 (not_9_out, I_14);
  and and_6 (and_6_out, I_15, I_14);
  and and_7 (and_7_out, I_15, not_10_out);
  not not_10 (not_10_out, I_14);
  and and_8 (and_8_out, I_15, I_13);
  not not_11 (not_11_out, I_15);
  not not_12 (not_12_out, I_14);
  and and_9 (and_9_out, not_12_out, I_12);
  and and_10 (and_10_out, I_15, I_14);
  not not_13 (not_13_out, I_13);
  and and_11 (and_11_out, not_13_out, not_14_out);
  not not_14 (not_14_out, I_12);
  and and_12 (and_12_out, I_15, I_14);
  and and_13 (and_13_out, I_13, I_12);
  and and_14 (and_14_out, I_15, I_14);
  and and_15 (and_15_out, I_15, I_14);
  nand nand_8 (AS1, nand_1_out, nand_2_out);
  and and_16 (and_16_out, not_1_out, I_13);
  or or_1 (or_1_out, and_16_out, and_17_out);
  and and_17 (and_17_out, and_1_out, I_12);
  and and_18 (and_18_out, I_15, I_14);
  and and_19 (and_19_out, and_18_out, and_20_out);
  and and_20 (and_20_out, not_2_out, not_3_out);
  nand nand_9 (nand_9_out, I_15, I_15);
  and and_21 (and_21_out, I_15, nand_3_out);
  and and_22 (and_22_out, I_15, I_14);
  nand nand_10 (nand_10_out, I_13, I_13);
  nand nand_11 (nand_11_out, nand_4_out, I_13);
  and and_23 (and_23_out, I_14, nand_5_out);
  nand nand_12 (nand_12_out, I_12, I_12);
  nand nand_13 (nand_13_out, nand_6_out, I_13);
  and and_24 (and_24_out, I_14, nand_7_out);
  nand nand_14 (nand_14_out, I_12, I_12);
  not not_15 (not_15_out, I_15);
  and and_25 (and_25_out, and_2_out, not_6_out);
  or or_2 (or_2_out, and_3_out, and_4_out);
  and and_26 (and_26_out, I_13, I_12);
  and and_27 (and_27_out, and_5_out, I_12);
  and and_28 (and_28_out, and_6_out, I_13);
  and and_29 (and_29_out, and_7_out, I_13);
  and and_30 (and_30_out, and_8_out, I_12);
  or or_3 (BRANCH_SELECT, not_11_out, and_9_out);
  and and_31 (and_31_out, and_10_out, and_11_out);
  and and_32 (and_32_out, and_12_out, and_13_out);
  and and_33 (and_33_out, and_14_out, I_12);
  or or_4 (Imm_select, and_33_out, and_34_out);
  and and_34 (and_34_out, and_15_out, I_13);
  or or_5 (AS2, or_1_out, and_19_out);
  nand nand_15 (nand_15_out, nand_9_out, I_12);
  nand nand_16 (nand_16_out, I_14, I_12);
  nand nand_17 (nand_17_out, and_21_out, I_13);
  nand nand_18 (nand_18_out, and_22_out, nand_10_out);
  and and_35 (and_35_out, I_15, nand_11_out);
  nand nand_19 (nand_19_out, and_23_out, nand_12_out);
  and and_36 (and_36_out, I_15, nand_13_out);
  nand nand_20 (nand_20_out, and_24_out, nand_14_out);
  or or_6 (or_6_out, not_15_out, and_25_out);
  and and_37 (and_37_out, I_14, I_12);
  or or_7 (offset_select, or_2_out, and_26_out);
  or or_8 (mem_write, and_27_out, and_28_out);
  or or_9 (BRANCH, and_29_out, and_30_out);
  or or_10 (Jump_select, and_31_out, and_32_out);
  and and_38 (and_38_out, nand_15_out, nand_16_out);
  and and_39 (and_39_out, nand_17_out, nand_18_out);
  nand nand_21 (SA_SELECT, and_35_out, nand_19_out);
  nand nand_22 (WD_SELECT, and_36_out, nand_20_out);
  or or_11 (WE, or_6_out, and_37_out);
  nand nand_23 (AS3, and_38_out, and_39_out);
endmodule

module Main (
  input  in_1
);

  wire and_1_out, CLK_out, CU_branch, CU_branch_select, CU_imm_select, CU_jump_select, CU_mem_write,
       CU_offset_select, CU_sa_select, CU_wd_select, CU_we, multiplexer_6_out, not_1_out, or_1_out, or_2_out;
  wire [2:0] CU_as3;
  wire [3:0] multiplexer_2_out;
  wire [15:0] adder_1_out, adder_2_out, alu_1_alu_output, bit_extender_1_out, bit_extender_2_out,
       bit_extender_3_out, multiplexer_1_out, multiplexer_3_out, multiplexer_4_out, multiplexer_5_out,
       multiplexer_7_out, multiplexer_8_out, ram_1_data, register_1_q, register_bank_1_rd_1,
       register_bank_1_rd_2, rom_1_data;

  Register #(.width(16)) register_1 (.D(multiplexer_1_out), .Q(register_1_q), .clk(CLK_out), .clr(in_1));  // open: en
  Multiplexer #(.width(16), .enable("false")) multiplexer_1 (
    .in0(adder_1_out), .in1(adder_2_out), .out(multiplexer_1_out), .sel(or_1_out));
  Clock CLK (.out(CLK_out));
  or or_1 (or_1_out, and_1_out, CU_jump_select);
  and and_1 (and_1_out, multiplexer_6_out, CU_branch);
  Adder #(.width(16)) adder_1 (.a(register_1_q), .b(16'h1), .out(adder_1_out));  // open: cin, cout
  ROM #(.addrWidth(16), .dataWidth(16)) rom_1 (.addr(register_1_q), .data(rom_1_data));  // open: sel
  control_unit CU (
    .I_15(rom_1_data[15]), .I_14(rom_1_data[14]), .I_13(rom_1_data[13]), .I_12(rom_1_data[12]),
    .AS1(CU_as3[2]), .AS2(CU_as3[1]), .AS3(CU_as3[0]), .SA_SELECT(CU_sa_select), .WD_SELECT(CU_wd_select),
    .WE(CU_we), .offset_select(CU_offset_select), .mem_write(CU_mem_write), .BRANCH(CU_branch),
    .BRANCH_SELECT(CU_branch_select), .Jump_select(CU_jump_select), .Imm_select(CU_imm_select));
  Multiplexer #(.width(4), .enable("false")) multiplexer_2 (
    .in0(rom_1_data[3:0]), .in1(rom_1_data[11:8]), .out(multiplexer_2_out), .sel(CU_offset_select));
  assign bit_extender_1_out = {{12{1'b0}}, multiplexer_2_out};  // Bit_Extender bit_extender_1
  register_bank register_bank_1 (
    .Write_data(multiplexer_3_out), .Select_Ra_1(rom_1_data[3:0]), .Select_Ra_2(rom_1_data[7:4]),
    .Write_enable(CU_we), .Rd_1(register_bank_1_rd_1), .Rd_2(register_bank_1_rd_2), .clock(CLK_out),
    .Write_Register(rom_1_data[11:8]));
  Multiplexer #(.width(16), .enable("false")) multiplexer_3 (
    .in0(multiplexer_8_out), .in1(16'h990), .out(multiplexer_3_out), .sel(CU_imm_select));
  assign bit_extender_2_out = {{12{rom_1_data[11]}}, rom_1_data[11:8]};  // Bit_Extender bit_extender_2
  assign bit_extender_3_out = {{4{rom_1_data[11]}}, rom_1_data[11:0]};  // Bit_Extender bit_extender_3
  Multiplexer #(.width(16), .enable("false")) multiplexer_4 (
    .in0(bit_extender_1_out), .in1(register_bank_1_rd_1), .out(multiplexer_4_out), .sel(CU_sa_select));
  Multiplexer #(.width(16), .enable("false")) multiplexer_5 (
    .in0(bit_extender_2_out), .in1(bit_extender_3_out), .out(multiplexer_5_out), .sel(CU_jump_select));
  Multiplexer #(.enable("false")) multiplexer_6 (
    .in0(not_1_out), .in1(or_2_out), .out(multiplexer_6_out), .sel(CU_branch_select));
  ALU alu_1 (
    .A(multiplexer_4_out), .B(register_bank_1_rd_2), .alu_select(CU_as3), .alu_output(alu_1_alu_output));  // open: carry_in_adder, carry_in_sub, multiply_carry_in, divider_carry_in, carry_out_adder, carry_out_sub, multiply_carry_out, divider_Carry_out
  Multiplexer #(.width(16), .enable("false")) multiplexer_7 (
    .in0(register_bank_1_rd_1), .in1(16'h990), .out(multiplexer_7_out), .sel(CU_imm_select));
  Multiplexer #(.width(16), .enable("false")) multiplexer_8 (
    .in0(ram_1_data), .in1(alu_1_alu_output), .out(multiplexer_8_out), .sel(CU_wd_select));
  Adder #(.width(16)) adder_2 (.a(register_1_q), .b(multiplexer_5_out), .out(adder_2_out));  // open: cin, cout
  not not_1 (not_1_out, or_2_out);
  or or_2 (or_2_out, alu_1_alu_output[0], alu_1_alu_output[1], alu_1_alu_output[2], alu_1_alu_output[3], alu_1_alu_output[4], alu_1_alu_output[5], alu_1_alu_output[6], alu_1_alu_output[7], alu_1_alu_output[8], alu_1_alu_output[9], alu_1_alu_output[10], alu_1_alu_output[11], alu_1_alu_output[12], alu_1_alu_output[13], alu_1_alu_output[14], alu_1_alu_output[15]);
  RAM #(.addrWidth(16), .dataWidth(16), .bus("separate")) ram_1 (
    .addr(alu_1_alu_output), .din(multiplexer_7_out), .data(ram_1_data), .str(CU_mem_write), .sel(1'b1),
    .clk(CLK_out), .ld(1'b1));  // open: clr

  // Notes on the sheet:
  //   pc select
  //         Jump select
  //                                                      Instruction Memory         
  //                branch
  //   contents of rom_1 (hex, n*v repeats v):
  //   e300 d300
  //   CONDITION
  //                             Opcode
  //         OS
  //            Imm_s
  //   BO
  //   JO
  //   Jump select
  //        SA_S
  //             RD1
  //                          WD SELECT
  //   beq
  //   bne
  //   Alu output
  //   RAM
endmodule
